// Logisim project d8421plus1.circ as structural Verilog: 1 circuit, main circuit D8421plus1
module D8421plus1 (
  input  [3:0] D8421,
  output [3:0] D8421_1
);

  wire and_1_out, and_2_out, and_3_out, and_4_out, and_5_out, and_6_out, not_1_out, not_2_out, not_3_out,
       not_4_out, not_5_out;

  // Probe on D8421
  and and_1 (and_1_out, D8421[2], D8421[1], D8421[0]);
  not not_1 (not_1_out, D8421[2]);
  not not_2 (not_2_out, D8421[1]);
  not not_3 (not_3_out, D8421[0]);
  not not_4 (not_4_out, D8421[1]);
  not not_5 (not_5_out, D8421[0]);
  not not_6 (D8421_1[0], D8421[0]);
  or or_1 (D8421_1[3], and_1_out, D8421[3]);
  and and_2 (and_2_out, not_1_out, D8421[1], D8421[0]);
  and and_3 (and_3_out, D8421[2], not_2_out);
  and and_4 (and_4_out, D8421[2], not_3_out);
  and and_5 (and_5_out, not_4_out, D8421[0]);
  and and_6 (and_6_out, D8421[1], not_5_out);
  or or_2 (D8421_1[2], and_2_out, and_3_out, and_4_out);
  or or_3 (D8421_1[1], and_5_out, and_6_out);
  // Probe on D8421_1
endmodule
