// Logisim project binary_counter.circ as structural Verilog: 1 circuit, main circuit main
module main (
  output [2:0] Q1Q2Q3
);

  wire and_1_out, clock_1_out;

  Clock clock_1 (.out(clock_1_out));
  T_Flip_Flop t_ff_1 (.clk(clock_1_out), .T(1'b1), .Q(Q1Q2Q3[0]));  // open: Qn, preset, reset, en
  T_Flip_Flop t_ff_2 (.clk(clock_1_out), .T(Q1Q2Q3[0]), .Q(Q1Q2Q3[1]));  // open: Qn, preset, reset, en
  and and_1 (and_1_out, Q1Q2Q3[1], Q1Q2Q3[0]);
  T_Flip_Flop t_ff_3 (.clk(clock_1_out), .T(and_1_out), .Q(Q1Q2Q3[2]));  // open: Qn, preset, reset, en

  // Notes on the sheet:
  //   V
  //   Q3
  //   h3
  //   h2
  //   Q2
  //   h1
  //   Q1
endmodule
